# Fritzing sketch IndorWeather (saved by Fritzing 0.9.6b)
circuit board: 8.46667cm x 5.64444cm
breadboards: 1

parts:
  Bauteil1 = Arduino Nano (Rev3.0)
  Bauteil2 = NRF24L01+ Breakout Board
  RHT1 = Humidity and Temperature Sensor RHT03
  Part1 = KY-022 Infrared Receiver Module [package="Breakout board"]

nets (from the pcb view):
  GND: Bauteil1.GND, Bauteil2.GND, RHT1.GND_2, Part1.-
  N1: Bauteil1.D6, Part1.S
  N2: Bauteil1.D8, Bauteil2.MISO
  N3: Bauteil1.D9, Bauteil2.CS
  N4: Bauteil1.D10, Bauteil2.CE
  N5: Bauteil1.D11/MOSI, Bauteil2.MOSI
  N6: Bauteil1.D12/MISO, RHT1.Data-signal
  5V: Bauteil1.5V, RHT1.Vcc, Part1.Vin
  3V3: Bauteil1.3V3, Bauteil2.VCC
  N7: Bauteil1.D13/SCK, Bauteil2.SCK

custom parts:
  KY-022 Infrared Receiver Module: Arduino IR receiver module KY-022, based on 1838 IR Receiver/Decoder. It reacts to 38kHz infrared light.

// code stored in the sketch: outdoorWeather.ino



/*
  Arduino Wireless Communication Tutorial
      Outdoor unit - Transmitter

  by Dejan Nedelkovski, www.HowToMechatronics.com

  Libraries:
  NRF24L01 - TMRh20/RF24, https://github.com/tmrh20/RF24/
  DHT22 - DHTlib, https://github.com/RobTillaart/Arduino/tree/master/libraries/DHTlib
  LowPower - https://github.com/rocketscream/Low-Power
*/
#include <SPI.h>
#include <nRF24L01.h>
#include <RF24.h>
#include <DHT.h>
#include <Servo.h>
#include "IRremote.h"
#include <LowPower.h>

#define DHTPIN 8 // Ich nutze Digital-PIN 8
#define DHTTYPE DHT22 // DHT 22 (AM2302)
DHT dht(DHTPIN, DHTTYPE);
int receiver = 6;

RF24 radio(10, 9); // CE, CSN
const byte address[6] = "00001";

char thChar[32] = "";
String thString = "";
bool autoMode = true;
bool isOpen = false;


Servo myservo;
IRrecv irrecv(receiver);
decode_results results;


void setup() {
  radio.begin();
  radio.openWritingPipe(address);
  radio.setPALevel(RF24_PA_MIN);
  radio.stopListening();
  Serial.begin(9600);
   dht.begin();
   myservo.attach(2);//connect pin 2 with the control line(the middle line of Servo) 
  irrecv.enableIRIn(); // Start the receiver
 

}
void loop() {

float h = dht.readHumidity();
float t = dht.readTemperature();

if (irrecv.decode(&results)) // have we received an IR signal?
{Serial.println(results.value, HEX);
    switch(results.value)
    
    {

      case 0xFF906F: // Up button pressed
      Serial.println("Vol+ pressed");
                    openServo();
                     delay(1000);
                   
                      break;

      case 0xFFE01F: // Down button pressed
       Serial.println("Vol- pressed");
                     closeServo();
                      delay(1000);
                     
                      break;              
       case 0xFF02FD: // pause Auto
       autoMode = !autoMode;
       delay(1000);         
    }
    
      irrecv.resume(); // receive the next value
        
  }  


openRoof(t,h);

if (isnan(h) || isnan(t)) {       
    Serial.println("Fehler beim auslesen des Sensors!");
    closeServo();
    thString = String("E") + String("R");
    thString.toCharArray(thChar, 12);
    radio.write(&thChar, sizeof(thChar));
    return;
  }
   Serial.print("Luftfeuchtigkeit: ");
  Serial.print(h);                  // Ausgeben der Luftfeuchtigkeit
  Serial.print("%\t");              // Tabulator
  Serial.print("Temperatur: ");
  Serial.print(t);                  // Ausgeben der Temperatur
  Serial.write('°');                // Schreiben des ° Zeichen
  Serial.println("C");

  thString = String(t) + String(h) + String(autoMode);
  thString.toCharArray(thChar, 12);
  // Sent the data wirelessly to the indoor unit
  for (int i = 0; i <= 3; i++) {  // Send the data 3 times
    radio.write(&thChar, sizeof(thChar));
    delay(50);
  }

  for (int sleepCounter = 37; sleepCounter > 0; sleepCounter--)
  {
    LowPower.powerDown(SLEEP_8S, ADC_OFF, BOD_OFF);
  }


}

void openRoof(float temp, float floathumid) {

  if(temp >= 15 && autoMode == true){ 
    openServo();
  }else if( temp < 13 && autoMode == true) {
    closeServo();
  }

}

void openServo(){
  if(isOpen == false) {
     myservo.write(0);
  delay(1000);
  myservo.write(90);
  isOpen = true;
  }
}

void closeServo(){
  if(isOpen == true){
     myservo.write(180);
  delay(1000);
  myservo.write(90);
  isOpen = false;
  }
}
